// Logisim project Lab1_Logisim_Demo.circ as structural Verilog: 3 circuits, main circuit main
module main (
  input  [17:0] SW,
  input  s,
  input  [7:0] x,
  input  [7:0] m,
  input  [7:0] y,
  output [17:0] LEDR
);

  mux2to1 mux2to1_1 (.x(x[0]), .y(y[0]), .s(s), .m(m[0]));
  mux2to1 mux2to1_2 (.x(x[1]), .y(y[1]), .s(s), .m(m[1]));
  mux2to1 mux2to1_3 (.x(x[2]), .y(y[2]), .s(s), .m(m[2]));
  mux2to1 mux2to1_4 (.x(x[3]), .y(y[3]), .s(s), .m(m[3]));
  mux2to1 mux2to1_5 (.x(x[4]), .y(y[4]), .s(s), .m(m[4]));
  mux2to1 mux2to1_6 (.x(x[5]), .y(y[5]), .s(s), .m(m[5]));
  mux2to1 mux2to1_7 (.x(x[6]), .y(y[6]), .s(s), .m(m[6]));
  mux2to1 mux2to1_8 (.x(x[7]), .y(y[7]), .s(s), .m(m[7]));

  assign LEDR = SW;
endmodule

module mux2to1 (
  input  x,
  input  y,
  input  s,
  output m
);

  wire and_1_out, and_2_out, not_1_out;

  not not_1 (not_1_out, s);
  and and_1 (and_1_out, x, not_1_out);
  and and_2 (and_2_out, y, s);
  or or_1 (m, and_1_out, and_2_out);
endmodule

module mux5to1_3bit (
  input  u,
  input  v
);

  mux2to1 mux2to1_1 (.x(u), .y(v));  // open: s, m
  mux2to1 mux2to1_2 (.x(u), .y(v));  // open: s, m
  mux2to1 mux2to1_3 ();  // open: x, y, s, m
  mux2to1 mux2to1_4 ();  // open: x, y, s, m
endmodule
